# Fritzing sketch Multiplex (saved by Fritzing 0.9.2b)
perfboards: 1

parts:
  R1 = Rotary Potentiometer (Small) [maximum_resistance=100kΩ package=THT]
  R2 = Rotary Potentiometer (Small) [maximum_resistance=100kΩ package=THT]
  R3 = Rotary Potentiometer (Small) [maximum_resistance=100kΩ package=THT]
  R4 = Rotary Potentiometer (Small) [maximum_resistance=100kΩ package=THT]
  R5 = Rotary Potentiometer (Small) [maximum_resistance=100kΩ package=THT]
  R6 = Rotary Potentiometer (Small) [maximum_resistance=100kΩ package=THT]
  R7 = Rotary Potentiometer (Small) [maximum_resistance=100kΩ package=THT]
  R8 = Rotary Potentiometer (Small) [maximum_resistance=100kΩ package=THT]
  IC1 = IC, DIP package, 16 pins [chip_label=CD4051BE]
  Part1 = Arduino Uno (Rev3) - ICSP

nets:
  N1: R1.leg1, R2.leg1, R3.leg1, R4.leg1, R5.leg1, R6.leg1, R7.leg1, R8.leg1, IC1.pin6, IC1.pin7, IC1.pin8, Part1.GND
  N2: R1.wiper, IC1.pin13
  N3: R1.leg2, R2.leg2, R3.leg2, R4.leg2, R5.leg2, R6.leg2, R7.leg2, R8.leg2, IC1.pin16, Part1.5V
  N4: R2.wiper, IC1.pin14
  N5: R3.wiper, IC1.pin15
  N6: R4.wiper, IC1.pin12
  N7: R5.wiper, IC1.pin1
  N8: R6.wiper, IC1.pin5
  N9: R7.wiper, IC1.pin2
  N10: R8.wiper, IC1.pin4
  N11: IC1.pin3, Part1.A0
  N12: IC1.pin9, Part1.D4
  N13: IC1.pin10, Part1.D3_PWM
  N14: IC1.pin11, Part1.D2
